# Fritzing sketch PlanoCircuito (saved by Fritzing 0.7.11b)
breadboards: 1

parts:
  Arduino1 = Arduino
  R1 = Photocell (LDR) [package=THT]
  R2 = 4200 Ω Resistor [package=THT]
  R3 = Resistor [tolerance=±5% resistance=220 package=THT]
  R4 = Resistor [tolerance=±5% resistance=220 package=THT]
  R5 = Resistor [tolerance=±5% resistance=220 package=THT]
  R6 = Resistor [tolerance=±5% resistance=220 package=THT]
  LED1 = LED - 5mm [color="Red (633nm)" package="5 mm [THT]"]
  LED2 = LED - 5mm [color="Red (633nm)" package="5 mm [THT]"]
  LED3 = LED - 5mm [color="Red (633nm)" package="5 mm [THT]"]
  LED4 = LED - 5mm [color="Red (633nm)" package="5 mm [THT]"]

nets:
  N1: Arduino1.D12, LED1.cathode
  N2: Arduino1.D11, LED2.cathode
  N3: Arduino1.D10, LED3.cathode
  N4: Arduino1.D9, LED4.cathode
  N5: Arduino1.+5V, R1.pin_0
  N6: Arduino1.GND, R2.Pin_1, R3.Pin_1, R4.Pin_1, R5.Pin_1, R6.Pin_1
  N7: Arduino1.A0, R1.pin_1, R2.Pin_0
  N8: R3.Pin_0, LED1.anode
  N9: R4.Pin_0, LED2.anode
  N10: R5.Pin_0, LED3.anode
  N11: R6.Pin_0, LED4.anode

notes:
  Ojo que la resistencia del sensor de luz es de 4.200

custom parts:
  4200 Ω Resistor: A generic resistor (0.25W)
