# Fritzing sketch plano (saved by Fritzing 0.7.11b)
breadboards: 1

parts:
  Arduino1 = Arduino
  R1 = Slide Potentiometer [maximum_resistance=100kΩ]
  LED1 = LED - 5mm [color="Red (633nm)" package="5 mm [THT]"]
  R2 = Resistor [tolerance=±5% resistance=220 package=THT]

nets:
  N1: Arduino1.GND, R1.leg2, R2.Pin_1
  N2: Arduino1.D13, LED1.anode, R2.Pin_0
  N3: Arduino1.+5V, R1.leg1, LED1.cathode
  N4: Arduino1.A0, R1.wiper
